// Logisim project muCPU[rev1].circ as structural Verilog: 10 circuits, main circuit main
module main (
);

  wire and_1_out, and_4_out, and_7_out, bit_extender_3_out, clock_1_out, comparator_1_eq, decoder_1_out0,
       decoder_1_out1, decoder_1_out2, decoder_1_out3, decoder_2_out1, decoder_2_out2, decoder_2_out3,
       mem_en, not_1_out, not_2_out, or_1_out, or_2_out, or_3_out, or_4_out, or_5_out, or_6_out, write_to_mem;
  wire [1:0] controlled_buffer_2_out, counter_1_q, multiplexer_5_out;
  wire [2:0] and_2_out, bit_extender_1_out;
  wire [7:0] adder_1_out, adder_2_out, adder_3_out, adder_4_out, bit_extender_2_out, data_from_mem,
       data_to_mem, IR_q_2, mem_address, multiplexer_1_out, multiplexer_2_out, multiplexer_3_out,
       multiplexer_6_out, multiplexer_8_out, multiplexer_9_out, nand_1_out, PCnext_q, r1_q, r2_q, r3_q,
       register_1_q, shift_register_1_q0, shift_register_1_q1, shifter_1_out;
  wire [15:8] IR_q;

  Multiplexer #(.width(8), .disabled(0), .enable("false")) multiplexer_1 (
    .in0(adder_1_out), .in1(multiplexer_8_out), .out(multiplexer_1_out), .sel(decoder_1_out2));
  or or_1 (or_1_out, decoder_1_out2, or_2_out);
  Adder adder_1 (.a(8'h1), .b(register_1_q), .out(adder_1_out));  // open: cin, cout
  Register register_1 (.D(multiplexer_1_out), .en(or_1_out), .Q(register_1_q), .clk(clock_1_out));  // open: clr
  Multiplexer #(.width(8), .disabled(0), .enable("false")) multiplexer_2 (
    .in0(register_1_q), .in1(mem_address), .out(multiplexer_2_out), .sel(mem_en));
  not not_1 (not_1_out, write_to_mem);
  Clock clock_1 (.out(clock_1_out));
  assign data_from_mem = write_to_mem ? data_to_mem : 8'bz;  // Controlled_Buffer controlled_buffer_1
  RAM ram_1 (
    .addr(multiplexer_2_out), .data(data_from_mem), .sel(1'b1), .clk(clock_1_out), .ld(not_1_out));  // open: clr
  Decoder #(.select(2), .disabled(0), .enable("false")) decoder_1 (
    .out0(decoder_1_out0), .out1(decoder_1_out1), .out2(decoder_1_out2), .out3(decoder_1_out3),
    .sel(counter_1_q));
  Counter #(.width(2), .max('h3)) counter_1 (
    .count(1'b1), .Q(counter_1_q), .clk(clock_1_out));  // open: load, D, carry, clr
  Shift_Register #(.width(8), .length(2)) shift_register_1 (
    .shift(or_2_out), .in(data_from_mem), .clk(clock_1_out), .q0(shift_register_1_q0),
    .q1(shift_register_1_q1));  // open: out, load, clr, d0, d1
  or or_2 (or_2_out, decoder_1_out0, decoder_1_out1);
  Decoder #(.select(2), .disabled(0)) decoder_2 (
    .out1(decoder_2_out1), .out2(decoder_2_out2), .out3(decoder_2_out3), .sel(IR_q[11:10]), .en(and_7_out));  // open: out0
  // Probe on {shift_register_1_q1, shift_register_1_q0}
  Register #(.width(16)) IR (
    .D({shift_register_1_q1, shift_register_1_q0}), .en(decoder_1_out3), .Q({IR_q, IR_q_2}), .clk(clock_1_out));  // open: clr
  Register PCnext (.D(register_1_q), .en(decoder_1_out3), .Q(PCnext_q), .clk(clock_1_out));  // open: clr
  or or_3 (or_3_out, decoder_1_out2, decoder_1_out3);
  Register r1 (.D(multiplexer_9_out), .en(decoder_2_out1), .Q(r1_q), .clk(clock_1_out));  // open: clr
  and and_1 (and_1_out, IR_q[12], IR_q[13], ~IR_q[14]);  // AND_Gate
  and and_2 (and_2_out[0], ~IR_q[12], ~IR_q[13], IR_q[14]);  // AND_Gate
  or or_4 (or_4_out, and_1_out, and_2_out[0], and_2_out[2]);
  and and_3 (and_2_out[2], IR_q[12], ~IR_q[13], IR_q[14]);  // AND_Gate
  Register r2 (.D(multiplexer_9_out), .en(decoder_2_out2), .Q(r2_q), .clk(clock_1_out));  // open: clr
  Register r3 (.D(multiplexer_9_out), .en(decoder_2_out3), .Q(r3_q), .clk(clock_1_out));  // open: clr
  nor nor_1 (and_2_out[1], and_1_out, and_2_out[2]);
  Multiplexer #(.select(2), .width(8), .disabled(0), .enable("false")) multiplexer_3 (
    .in0({8{1'b0}}), .in1(r1_q), .in2(r2_q), .in3(r3_q), .out(multiplexer_3_out), .sel(IR_q[9:8]));
  Multiplexer #(.select(2), .width(8), .disabled(0), .enable("false")) multiplexer_4 (
    .in0({8{1'b0}}), .in1(r1_q), .in2(r2_q), .in3(r3_q), .out(data_to_mem), .sel(multiplexer_5_out));
  Multiplexer #(.width(2), .disabled(0), .enable("false")) multiplexer_5 (
    .in0(IR_q_2[7:6]), .in1(IR_q[11:10]), .out(multiplexer_5_out), .sel(or_4_out));
  assign controlled_buffer_2_out = not_2_out ? IR_q[13:12] : 2'bz;  // Controlled_Buffer controlled_buffer_2
  not not_2 (not_2_out, and_2_out[0]);
  assign controlled_buffer_2_out = and_2_out[0] ? 2'b01 : 2'bz;  // Controlled_Buffer controlled_buffer_3
  Bit_Extender #(.out_width(3)) bit_extender_1 (.in(multiplexer_6_out), .out(bit_extender_1_out));
  Multiplexer #(.width(8), .disabled(0), .enable("false")) multiplexer_6 (
    .in0(data_to_mem), .in1(IR_q_2), .out(multiplexer_6_out), .sel(or_5_out));
  or or_5 (or_5_out, and_2_out[0], and_2_out[2]);
  Shifter shifter_1 (.in(multiplexer_3_out), .\dist (bit_extender_1_out), .out(shifter_1_out));
  Adder adder_2 (.a(multiplexer_3_out), .b(multiplexer_6_out), .out(adder_2_out));  // open: cin, cout
  assign nand_1_out = ~(multiplexer_3_out & multiplexer_6_out);  // NAND_Gate nand_1, 8 bits wide
  Comparator comparator_1 (.a(multiplexer_3_out), .b(multiplexer_6_out), .eq(comparator_1_eq));  // open: gt, lt
  assign bit_extender_2_out = {{7{1'b0}}, comparator_1_eq};  // Bit_Extender bit_extender_2
  Bit_Extender #(.out_width(1)) bit_extender_3 (.in(mem_address), .out(bit_extender_3_out));
  Multiplexer #(.select(2), .width(8), .disabled(0), .enable("false")) multiplexer_7 (
    .in0(shifter_1_out), .in1(adder_2_out), .in2(nand_1_out), .in3(bit_extender_2_out), .out(mem_address),
    .sel(controlled_buffer_2_out));
  and and_4 (and_4_out, controlled_buffer_2_out[0], controlled_buffer_2_out[1], bit_extender_3_out);
  and and_5 (write_to_mem, and_2_out[2], or_3_out);
  Adder adder_3 (.a(8'h2), .b(PCnext_q), .out(adder_3_out));  // open: cin, cout
  Multiplexer #(.width(8), .disabled(0), .enable("false")) multiplexer_8 (
    .in0(adder_3_out), .in1(adder_4_out), .out(multiplexer_8_out), .sel(and_4_out));
  Adder adder_4 (.a(PCnext_q), .b(IR_q_2), .out(adder_4_out));  // open: cin, cout
  Multiplexer #(.width(8), .disabled(0), .enable("false")) multiplexer_9 (
    .in0(mem_address), .in1(data_from_mem), .out(multiplexer_9_out), .sel(and_2_out[0]));
  or or_6 (or_6_out, and_2_out[2], and_2_out[0]);
  and and_6 (mem_en, or_6_out, or_3_out);
  and and_7 (and_7_out, and_2_out[1], decoder_1_out3);

  // Notes on the sheet:
  //   Instruction Access [t0-t1] RAM Access [t2-t3]
  //   REGISTER FILE
  //   rt
  //   wb enable
  //   rs
  //   opcode
endmodule

module ALU (
  input  [3:0] s,
  input  [3:0] t,
  input  [1:0] opcode,
  output [3:0] result
);

  wire comparator_1_eq;
  wire [1:0] bit_extender_1_out;
  wire [3:0] adder_1_out, bit_extender_2_out, nand_1_out, shifter_1_out;

  Bit_Extender #(.in_width(4), .out_width(2)) bit_extender_1 (.in(t), .out(bit_extender_1_out));
  Shifter #(.width(4)) shifter_1 (.in(s), .\dist (bit_extender_1_out), .out(shifter_1_out));
  Adder #(.width(4)) adder_1 (.a(s), .b(t), .out(adder_1_out));  // open: cin, cout
  assign nand_1_out = ~(s & t);  // NAND_Gate nand_1, 4 bits wide
  assign bit_extender_2_out = {{3{1'b0}}, comparator_1_eq};  // Bit_Extender bit_extender_2
  Comparator #(.width(4)) comparator_1 (.a(s), .b(t), .eq(comparator_1_eq));  // open: gt, lt
  Multiplexer #(.select(2), .width(4), .disabled(0), .enable("false")) multiplexer_1 (
    .in0(shifter_1_out), .in1(adder_1_out), .in2(nand_1_out), .in3(bit_extender_2_out), .out(result),
    .sel(opcode));
endmodule

module hex_encoder_for_vhdl (
  input  [3:0] opcode_opcode,
  input  [1:0] rd_rt,
  input  [1:0] rs_rs,
  input  [1:0] rt,
  input  [5:0] in_5,
  input  [7:0] imm,
  output [15:0] instruction
);

  wire and_1_out, and_2_out, and_3_out, and_4_out, not_1_out, or_1_out;

  // Probe on instruction
  Multiplexer #(.width(16), .disabled(0), .enable("false")) multiplexer_1 (
    .in0({opcode_opcode, rd_rt, rs_rs, imm}), .in1({opcode_opcode, rd_rt, rs_rs, rt, in_5}),
    .out(instruction), .sel(not_1_out));
  and and_1 (and_1_out, opcode_opcode[0], ~opcode_opcode[1], opcode_opcode[2], ~opcode_opcode[3]);  // AND_Gate
  and and_2 (and_2_out, ~opcode_opcode[0], opcode_opcode[1], opcode_opcode[2], ~opcode_opcode[3]);  // AND_Gate
  and and_3 (and_3_out, opcode_opcode[0], opcode_opcode[1], opcode_opcode[2], ~opcode_opcode[3]);  // AND_Gate
  and and_4 (and_4_out, ~opcode_opcode[0], ~opcode_opcode[1], ~opcode_opcode[2], opcode_opcode[3]);  // AND_Gate
  // Probe on instruction
  not not_1 (not_1_out, or_1_out);
  or or_1 (or_1_out, and_1_out, and_2_out, and_3_out, and_4_out);

  // Notes on the sheet:
  //   key: rtype/itype
  //   built for version 2 (vhdl only)
endmodule

module hex_encoder_for_v1 (
  input  [3:0] opcode_opcode,
  input  [1:0] rd_rt,
  input  [1:0] rs_rs,
  input  [1:0] rt,
  input  [5:0] in_5,
  input  [7:0] imm,
  output [15:0] instruction
);

  wire and_1_out, and_2_out, and_3_out, not_1_out, or_1_out;

  and and_1 (and_1_out, opcode_opcode[0], opcode_opcode[1], ~opcode_opcode[2]);  // AND_Gate
  and and_2 (and_2_out, ~opcode_opcode[0], ~opcode_opcode[1], opcode_opcode[2]);  // AND_Gate
  and and_3 (and_3_out, ~opcode_opcode[0], opcode_opcode[1], ~opcode_opcode[2]);  // AND_Gate
  Multiplexer #(.width(16), .disabled(0), .enable("false")) multiplexer_1 (
    .in0({opcode_opcode, rd_rt, rs_rs, imm}), .in1({opcode_opcode, rd_rt, rs_rs, rt, in_5}),
    .out(instruction), .sel(not_1_out));
  not not_1 (not_1_out, or_1_out);
  or or_1 (or_1_out, and_1_out, and_2_out, and_3_out);
  // Probe on instruction
  // Probe on instruction

  // Notes on the sheet:
  //   key: rtype/itype
  //   built for version 1 (the "main" circuit)
endmodule

module mem_prototype_for_vhdl (
  input  [7:0] in_1,
  input  in_2,
  input  [7:0] in_3,
  input  in_4,
  input  [7:0] in_5,
  input  in_6,
  input  [7:0] in_7,
  input  in_8,
  input  [7:0] in_9,
  input  in_10,
  input  [7:0] in_11,
  input  in_12,
  input  [7:0] in_13,
  input  in_14,
  input  [7:0] in_15,
  input  in_16,
  input  in_17,
  input  [7:0] data_in,
  input  [7:0] pc_in,
  input  [7:0] mem_addr,
  input  mem_access,
  input  mem_store,
  input  clk,
  input  [7:0] in_24,
  output [7:0] out_25,
  output out_26,
  output [7:0] out_27,
  output out_28,
  output [7:0] out_29,
  output out_30,
  output [7:0] out_31,
  output out_32,
  output [7:0] out_33,
  output out_34,
  output [7:0] out_35,
  output out_36,
  output [7:0] out_37,
  output out_38,
  output [7:0] out_39,
  output out_40,
  output [7:0] data_out
);

  wire and_1_out, and_2_out, and_3_out, decoder_1_out0, decoder_1_out1, decoder_1_out2, decoder_1_out3,
       decoder_1_out4, decoder_1_out5, decoder_1_out6, decoder_1_out7, not_1_out, not_2_out, not_3_out;
  wire [7:0] controlled_buffer_1_out, multiplexer_1_out, multiplexer_2_out, multiplexer_3_out,
       multiplexer_4_out, multiplexer_5_out, multiplexer_6_out, multiplexer_7_out, multiplexer_8_out,
       multiplexer_9_out, portA_q, portB_q, portC_q, portD_q, portE_q, portF_q, portG_q, portH_q,
       register_1_q, undriven;

  Multiplexer #(.width(8), .disabled(0), .enable("false")) multiplexer_1 (
    .in0(pc_in), .in1(mem_addr), .out(multiplexer_1_out), .sel(mem_access));
  Decoder #(.select(3), .disabled(0)) decoder_1 (
    .out0(decoder_1_out0), .out1(decoder_1_out1), .out2(decoder_1_out2), .out3(decoder_1_out3),
    .out4(decoder_1_out4), .out5(decoder_1_out5), .out6(decoder_1_out6), .out7(decoder_1_out7),
    .sel(multiplexer_1_out[2:0]), .en(and_1_out));
  and and_1 (and_1_out, mem_store, and_2_out);
  and and_2 (and_2_out, multiplexer_1_out[7], multiplexer_1_out[6], multiplexer_1_out[5], multiplexer_1_out[4], multiplexer_1_out[3]);
  not not_1 (not_1_out, multiplexer_1_out[7]);
  // Probe on in_24
  and and_3 (and_3_out, ~multiplexer_1_out[6], multiplexer_1_out[7]);  // AND_Gate
  not not_2 (not_2_out, mem_store);
  ROM #(.addrWidth(6)) rom_1 (.addr(multiplexer_1_out[5:0]), .data(data_out), .sel(and_3_out));
  RAM #(.addrWidth(7), .bus("separate")) ram_1 (
    .addr(multiplexer_1_out[6:0]), .din(data_in), .data(data_out), .str(mem_store), .sel(not_1_out),
    .clk(clk), .ld(not_2_out));  // open: clr
  Multiplexer #(.width(8), .disabled(0), .enable("false")) multiplexer_2 (
    .in0(in_1), .in1(undriven), .out(multiplexer_2_out), .sel(mem_store));
  Multiplexer #(.width(8), .disabled(0), .enable("false")) multiplexer_3 (
    .in0(in_3), .in1(undriven), .out(multiplexer_3_out), .sel(mem_store));
  Multiplexer #(.width(8), .disabled(0), .enable("false")) multiplexer_4 (
    .in0(in_5), .in1(undriven), .out(multiplexer_4_out), .sel(mem_store));
  Multiplexer #(.width(8), .disabled(0), .enable("false")) multiplexer_5 (
    .in0(in_7), .in1(undriven), .out(multiplexer_5_out), .sel(mem_store));
  Multiplexer #(.width(8), .disabled(0), .enable("false")) multiplexer_6 (
    .in0(in_9), .in1(undriven), .out(multiplexer_6_out), .sel(mem_store));
  Multiplexer #(.width(8), .disabled(0), .enable("false")) multiplexer_7 (
    .in0(in_11), .in1(undriven), .out(multiplexer_7_out), .sel(mem_store));
  Multiplexer #(.width(8), .disabled(0), .enable("false")) multiplexer_8 (
    .in0(in_13), .in1(undriven), .out(multiplexer_8_out), .sel(mem_store));
  Multiplexer #(.width(8), .disabled(0), .enable("false")) multiplexer_9 (
    .in0(in_15), .in1(undriven), .out(multiplexer_9_out), .sel(mem_store));
  Register portA (.D(multiplexer_2_out), .en(decoder_1_out0), .Q(portA_q), .clk(clk));  // open: clr
  Register portB (.D(multiplexer_3_out), .en(decoder_1_out1), .Q(portB_q), .clk(clk));  // open: clr
  Register portC (.D(multiplexer_4_out), .en(decoder_1_out2), .Q(portC_q), .clk(clk));  // open: clr
  Register portD (.D(multiplexer_5_out), .en(decoder_1_out3), .Q(portD_q), .clk(clk));  // open: clr
  Register portE (.D(multiplexer_6_out), .en(decoder_1_out4), .Q(portE_q), .clk(clk));  // open: clr
  Register portF (.D(multiplexer_7_out), .en(decoder_1_out5), .Q(portF_q), .clk(clk));  // open: clr
  Register portG (.D(multiplexer_8_out), .en(decoder_1_out6), .Q(portG_q), .clk(clk));  // open: clr
  Register portH (.D(multiplexer_9_out), .en(decoder_1_out7), .Q(portH_q), .clk(clk));  // open: clr
  Multiplexer #(.select(3), .width(8)) multiplexer_10 (
    .in0(portA_q), .in1(portB_q), .in2(portC_q), .in3(portD_q), .in4(portE_q), .in5(portF_q), .in6(portG_q),
    .in7(portH_q), .out(data_out), .sel(multiplexer_1_out[2:0]), .en(and_2_out));
  Decoder #(.select(3), .disabled(0)) decoder_2 (
    .sel(multiplexer_1_out[2:0]), .en(and_2_out));  // open: out0, out1, out2, out3, out4, out5, out6, out7
  not not_3 (not_3_out, in_17);
  assign controlled_buffer_1_out = not_3_out ? register_1_q : 8'bz;  // Controlled_Buffer controlled_buffer_1
  Register register_1 (.D(controlled_buffer_1_out), .Q(register_1_q));  // open: en, clk, clr
endmodule

module hex_encoder_for_vhdl_v2 (
  input  [1:0] opcode_opcode,
  input  [2:0] rd_rt,
  input  [2:0] rs_rs,
  input  [2:0] rt,
  input  [4:0] in_5,
  input  [7:0] imm,
  output [15:0] instruction
);

  wire and_1_out;

  // Probe on instruction
  Multiplexer #(.width(16), .disabled(0), .enable("false")) multiplexer_1 (
    .in0({opcode_opcode, rd_rt, rs_rs, imm}), .in1({opcode_opcode, rd_rt, rs_rs, rt, in_5}),
    .out(instruction), .sel(and_1_out));
  and and_1 (and_1_out, ~opcode_opcode[0], ~opcode_opcode[1]);  // AND_Gate
  // Probe on instruction

  // Notes on the sheet:
  //   key: rtype/itype
  //   built for version 2 (vhdl only)
endmodule

module spi_graphicsaccelerator (
  input  clk_in,
  input  reset,
  input  [7:0] command,
  input  [7:0] character,
  output mosi,
  output cs,
  output sclk,
  output d_c
);

  wire clock_1_out, counter_1_carry, counter_2_carry, counter_3_carry, counter_4_carry, decoder_1_out0,
       decoder_1_out1, decoder_1_out2, or_1_out, or_2_out, or_3_out, or_4_out, or_5_out, or_6_out,
       pc_reset_1_out_3, pc_reset_2_out_3, pc_reset_3_out_3, pc_reset_4_out_3, rising_edge_1_out_2,
       rising_edge_2_out_2, t_ff_1_q, t_ff_2_q, t_ff_3_q;
  wire [1:0] controlled_buffer_1_out, register_1_q;
  wire [2:0] counter_2_q;
  wire [4:0] counter_1_q;
  wire [7:0] multiplexer_2_out, multiplexer_3_out, ram_1_data, register_2_q, rom_1_data, rom_2_data;
  wire [9:0] counter_3_q, counter_4_q, multiplexer_1_out;

  Clock clock_1 (.out(clock_1_out));
  Register #(.width(2)) register_1 (
    .D(controlled_buffer_1_out), .en(or_1_out), .Q(register_1_q), .clk(or_1_out));  // open: clr
  or or_1 (or_1_out, or_6_out, rising_edge_2_out_2, rising_edge_1_out_2);
  or or_2 (or_2_out, rising_edge_1_out_2, pc_reset_1_out_3);
  or or_3 (or_3_out, rising_edge_1_out_2, pc_reset_2_out_3);
  or or_4 (or_4_out, rising_edge_1_out_2, pc_reset_3_out_3);
  or or_5 (or_5_out, rising_edge_1_out_2, pc_reset_4_out_3);
  Decoder #(.select(2), .enable("false")) decoder_1 (
    .out0(decoder_1_out0), .out1(decoder_1_out1), .out2(decoder_1_out2), .out3(d_c), .sel(register_1_q));
  rising_edge rising_edge_1 (.in_1(reset), .out_2(rising_edge_1_out_2));
  Counter #(.width(5), .max('h19)) counter_1 (
    .count(decoder_1_out0), .Q(counter_1_q), .carry(counter_1_carry), .clk(t_ff_3_q), .clr(or_2_out));  // open: load, D
  pc_reset pc_reset_1 (.in_2(t_ff_3_q), .out_3(pc_reset_1_out_3), .in_1(counter_1_carry));
  Counter #(.width(3), .max('h5)) counter_2 (
    .count(decoder_1_out2), .Q(counter_2_q), .carry(counter_2_carry), .clk(t_ff_3_q), .clr(or_3_out));  // open: load, D
  pc_reset pc_reset_2 (.in_2(t_ff_3_q), .out_3(pc_reset_2_out_3), .in_1(counter_2_carry));
  Counter #(.width(10), .max('h3ff)) counter_3 (
    .count(d_c), .Q(counter_3_q), .carry(counter_3_carry), .clk(t_ff_3_q), .clr(or_4_out));  // open: load, D
  pc_reset pc_reset_3 (.in_2(t_ff_3_q), .out_3(pc_reset_3_out_3), .in_1(counter_3_carry));
  Counter #(.width(10), .max('h3ff)) counter_4 (
    .count(decoder_1_out1), .Q(counter_4_q), .carry(counter_4_carry), .clk(clock_1_out), .clr(or_5_out));  // open: load, D
  pc_reset pc_reset_4 (.in_2(clock_1_out), .out_3(pc_reset_4_out_3), .in_1(counter_4_carry));
  or or_6 (or_6_out, counter_4_carry, counter_3_carry, counter_2_carry, counter_1_carry);
  assign controlled_buffer_1_out = rising_edge_2_out_2 ? 2'b01 : 2'bz;  // Controlled_Buffer controlled_buffer_1
  rising_edge rising_edge_2 (.in_1(command[7]), .out_2(rising_edge_2_out_2));
  Multiplexer #(.width(10), .enable("false")) multiplexer_1 (
    .in0(counter_3_q), .in1(counter_4_q), .out(multiplexer_1_out), .sel(decoder_1_out1));
  assign controlled_buffer_1_out = counter_4_carry ? 2'b10 : 2'bz;  // Controlled_Buffer controlled_buffer_2
  assign controlled_buffer_1_out = counter_3_carry ? 2'b00 : 2'bz;  // Controlled_Buffer controlled_buffer_3
  assign controlled_buffer_1_out = counter_2_carry ? 2'b11 : 2'bz;  // Controlled_Buffer controlled_buffer_4
  assign controlled_buffer_1_out = counter_1_carry ? 2'b10 : 2'bz;  // Controlled_Buffer controlled_buffer_5
  assign controlled_buffer_1_out = rising_edge_1_out_2 ? 2'b00 : 2'bz;  // Controlled_Buffer controlled_buffer_6
  ROM #(.addrWidth(5)) rom_1 (.addr(counter_1_q), .data(rom_1_data));  // open: sel
  ROM #(.addrWidth(3)) rom_2 (.addr(counter_2_q), .data(rom_2_data));  // open: sel
  RAM #(.addrWidth(10)) ram_1 (.addr(multiplexer_1_out), .data(ram_1_data));  // open: sel, clk, ld, clr
  Multiplexer #(.width(8), .disabled(0), .enable("false")) multiplexer_2 (
    .in0(rom_2_data), .in1(ram_1_data), .out(multiplexer_2_out), .sel(d_c));
  Multiplexer #(.width(8), .disabled(0), .enable("false")) multiplexer_3 (
    .in0(multiplexer_2_out), .in1(rom_1_data), .out(multiplexer_3_out), .sel(decoder_1_out0));
  T_Flip_Flop t_ff_1 (.clk(sclk), .T(sclk), .Q(t_ff_1_q));  // open: Qn, preset, reset, en
  Register register_2 (.D(multiplexer_3_out), .en(t_ff_3_q), .Q(register_2_q), .clk(t_ff_3_q));  // open: clr
  T_Flip_Flop t_ff_2 (.clk(t_ff_1_q), .T(t_ff_1_q), .Q(t_ff_2_q));  // open: Qn, preset, reset, en
  spi_master spi_master_1 (.data_in(register_2_q), .cs(1'b0), .clk50(clock_1_out), .mosi(mosi), .cs_2(cs), .sclk(sclk));
  T_Flip_Flop t_ff_3 (.clk(t_ff_2_q), .T(t_ff_2_q), .Q(t_ff_3_q));  // open: Qn, preset, reset, en

  // Notes on the sheet:
  //   Unfinished, used to write to buffer
  //   Init program
  //   Refresh program
  //   Buffer
  //   contents of rom_1 (hex, n*v repeats v):
  //   ae d5 80 a8 3f d3 0 40 8d 14 20 0 a1 c8 da 12 81 cf d9 f1 db 40 a4 a6 af
  //   contents of rom_2 (hex, n*v repeats v):
  //   21 0 7f 22 0 7
  //   SPI Master
  //   divide by 8
endmodule

module spi_master (
  input  [7:0] data_in,
  input  cs,
  input  clk50,
  output mosi,
  output cs_2,
  output sclk
);

  wire not_1_out, t_ff_1_q, t_ff_2_q;
  wire [2:0] counter_1_q;

  Multiplexer #(.select(3)) multiplexer_1 (
    .in0(data_in[7]), .in1(data_in[6]), .in2(data_in[5]), .in3(data_in[4]), .in4(data_in[3]),
    .in5(data_in[2]), .in6(data_in[1]), .in7(data_in[0]), .out(mosi), .sel(counter_1_q), .en(not_1_out));
  not not_1 (not_1_out, cs);
  Counter #(.width(3), .max('h7), .trigger("falling")) counter_1 (
    .Q(counter_1_q), .clk(sclk));  // open: load, D, count, carry, clr
  T_Flip_Flop t_ff_1 (.clk(clk50), .T(clk50), .Q(t_ff_1_q));  // open: Qn, preset, reset, en
  T_Flip_Flop t_ff_2 (.clk(t_ff_1_q), .T(t_ff_1_q), .Q(t_ff_2_q));  // open: Qn, preset, reset, en
  T_Flip_Flop t_ff_3 (.clk(t_ff_2_q), .T(t_ff_2_q), .Q(sclk));  // open: Qn, preset, reset, en

  assign cs_2 = cs;

  // Notes on the sheet:
  //   divide by 8
endmodule

module rising_edge (
  input  in_1,
  output out_2
);

  wire not_1_out;

  not not_1 (not_1_out, in_1);
  and and_1 (out_2, in_1, not_1_out);
endmodule

module pc_reset (
  input  in_1,
  input  in_2,
  output out_3
);

  wire not_1_out, rising_edge_1_out_2;

  and and_1 (out_3, in_1, rising_edge_1_out_2);
  not not_1 (not_1_out, in_2);
  rising_edge rising_edge_1 (.in_1(not_1_out), .out_2(rising_edge_1_out_2));
endmodule
