// Logisim project spi.circ as structural Verilog: 4 circuits, main circuit main
module main (
  input  clk_in,
  input  reset,
  input  [7:0] command,
  input  [7:0] character,
  output mosi,
  output cs,
  output sclk,
  output d_c
);

  wire counter_1_carry, counter_2_carry, counter_3_carry, counter_4_carry, decoder_1_out0, decoder_1_out1,
       decoder_1_out2, or_1_out, or_2_out, or_3_out, or_4_out, or_5_out, or_6_out, pc_reset_1_out_3,
       pc_reset_2_out_3, pc_reset_3_out_3, pc_reset_4_out_3, rising_edge_1_out_2, rising_edge_2_out_2,
       t_ff_1_q, t_ff_2_q, t_ff_3_q;
  wire [1:0] controlled_buffer_1_out, register_1_q;
  wire [2:0] counter_2_q;
  wire [4:0] counter_1_q;
  wire [7:0] multiplexer_2_out, multiplexer_3_out, ram_1_data, register_2_q, rom_1_data, rom_2_data;
  wire [9:0] counter_3_q, counter_4_q, multiplexer_1_out;

  Register #(.width(2)) register_1 (
    .D(controlled_buffer_1_out), .en(or_1_out), .Q(register_1_q), .clk(or_1_out));  // open: clr
  or or_1 (or_1_out, or_6_out, rising_edge_2_out_2, rising_edge_1_out_2);
  or or_2 (or_2_out, rising_edge_1_out_2, pc_reset_1_out_3);
  or or_3 (or_3_out, rising_edge_1_out_2, pc_reset_2_out_3);
  or or_4 (or_4_out, rising_edge_1_out_2, pc_reset_3_out_3);
  or or_5 (or_5_out, rising_edge_1_out_2, pc_reset_4_out_3);
  Decoder #(.select(2), .enable("false")) decoder_1 (
    .out0(decoder_1_out0), .out1(decoder_1_out1), .out2(decoder_1_out2), .out3(d_c), .sel(register_1_q));
  rising_edge rising_edge_1 (.in_1(reset), .out_2(rising_edge_1_out_2));
  Counter #(.width(5), .max('h19)) counter_1 (
    .count(decoder_1_out0), .Q(counter_1_q), .carry(counter_1_carry), .clk(t_ff_3_q), .clr(or_2_out));  // open: load, D
  pc_reset pc_reset_1 (.in_2(t_ff_3_q), .out_3(pc_reset_1_out_3), .in_1(counter_1_carry));
  Counter #(.width(3), .max('h5)) counter_2 (
    .count(decoder_1_out2), .Q(counter_2_q), .carry(counter_2_carry), .clk(t_ff_3_q), .clr(or_3_out));  // open: load, D
  pc_reset pc_reset_2 (.in_2(t_ff_3_q), .out_3(pc_reset_2_out_3), .in_1(counter_2_carry));
  Counter #(.width(10), .max('h3ff)) counter_3 (
    .count(d_c), .Q(counter_3_q), .carry(counter_3_carry), .clk(t_ff_3_q), .clr(or_4_out));  // open: load, D
  pc_reset pc_reset_3 (.in_2(t_ff_3_q), .out_3(pc_reset_3_out_3), .in_1(counter_3_carry));
  Counter #(.width(10), .max('h3ff)) counter_4 (
    .count(decoder_1_out1), .Q(counter_4_q), .carry(counter_4_carry), .clk(clk_in), .clr(or_5_out));  // open: load, D
  pc_reset pc_reset_4 (.in_2(clk_in), .out_3(pc_reset_4_out_3), .in_1(counter_4_carry));
  or or_6 (or_6_out, counter_4_carry, counter_3_carry, counter_2_carry, counter_1_carry);
  assign controlled_buffer_1_out = rising_edge_2_out_2 ? 2'b01 : 2'bz;  // Controlled_Buffer controlled_buffer_1
  rising_edge rising_edge_2 (.in_1(command[7]), .out_2(rising_edge_2_out_2));
  Multiplexer #(.width(10), .enable("false")) multiplexer_1 (
    .in0(counter_3_q), .in1(counter_4_q), .out(multiplexer_1_out), .sel(decoder_1_out1));
  assign controlled_buffer_1_out = counter_4_carry ? 2'b10 : 2'bz;  // Controlled_Buffer controlled_buffer_2
  assign controlled_buffer_1_out = counter_3_carry ? 2'b00 : 2'bz;  // Controlled_Buffer controlled_buffer_3
  assign controlled_buffer_1_out = counter_2_carry ? 2'b11 : 2'bz;  // Controlled_Buffer controlled_buffer_4
  assign controlled_buffer_1_out = counter_1_carry ? 2'b10 : 2'bz;  // Controlled_Buffer controlled_buffer_5
  assign controlled_buffer_1_out = rising_edge_1_out_2 ? 2'b00 : 2'bz;  // Controlled_Buffer controlled_buffer_6
  ROM #(.addrWidth(5)) rom_1 (.addr(counter_1_q), .data(rom_1_data));  // open: sel
  ROM #(.addrWidth(3)) rom_2 (.addr(counter_2_q), .data(rom_2_data));  // open: sel
  RAM #(.addrWidth(10)) ram_1 (.addr(multiplexer_1_out), .data(ram_1_data));  // open: sel, clk, ld, clr
  Multiplexer #(.width(8), .disabled(0), .enable("false")) multiplexer_2 (
    .in0(rom_2_data), .in1(ram_1_data), .out(multiplexer_2_out), .sel(d_c));
  Multiplexer #(.width(8), .disabled(0), .enable("false")) multiplexer_3 (
    .in0(multiplexer_2_out), .in1(rom_1_data), .out(multiplexer_3_out), .sel(decoder_1_out0));
  T_Flip_Flop t_ff_1 (.clk(sclk), .T(sclk), .Q(t_ff_1_q));  // open: Qn, preset, reset, en
  Register register_2 (.D(multiplexer_3_out), .en(t_ff_3_q), .Q(register_2_q), .clk(t_ff_3_q));  // open: clr
  T_Flip_Flop t_ff_2 (.clk(t_ff_1_q), .T(t_ff_1_q), .Q(t_ff_2_q));  // open: Qn, preset, reset, en
  spi_master spi_master_1 (.data_in(register_2_q), .cs(1'b0), .clk50(clk_in), .mosi(mosi), .cs_2(cs), .sclk(sclk));
  T_Flip_Flop t_ff_3 (.clk(t_ff_2_q), .T(t_ff_2_q), .Q(t_ff_3_q));  // open: Qn, preset, reset, en

  // Notes on the sheet:
  //   Unfinished, used to write to buffer
  //   Init program
  //   Refresh program
  //   Buffer
  //   contents of rom_1 (hex, n*v repeats v):
  //   ae d5 80 a8 3f d3 0 40 8d 14 20 0 a1 c8 da 12 81 cf d9 f1 db 40 a4 a6 af
  //   contents of rom_2 (hex, n*v repeats v):
  //   21 0 7f 22 0 7
  //   SPI Master
  //   divide by 8
endmodule

module spi_master (
  input  [7:0] data_in,
  input  cs,
  input  clk50,
  output mosi,
  output cs_2,
  output sclk
);

  wire not_1_out, t_ff_1_q, t_ff_2_q;
  wire [2:0] counter_1_q;

  Multiplexer #(.select(3)) multiplexer_1 (
    .in0(data_in[7]), .in1(data_in[6]), .in2(data_in[5]), .in3(data_in[4]), .in4(data_in[3]),
    .in5(data_in[2]), .in6(data_in[1]), .in7(data_in[0]), .out(mosi), .sel(counter_1_q), .en(not_1_out));
  not not_1 (not_1_out, cs);
  Counter #(.width(3), .max('h7), .trigger("falling")) counter_1 (
    .Q(counter_1_q), .clk(sclk));  // open: load, D, count, carry, clr
  T_Flip_Flop t_ff_1 (.clk(clk50), .T(clk50), .Q(t_ff_1_q));  // open: Qn, preset, reset, en
  T_Flip_Flop t_ff_2 (.clk(t_ff_1_q), .T(t_ff_1_q), .Q(t_ff_2_q));  // open: Qn, preset, reset, en
  T_Flip_Flop t_ff_3 (.clk(t_ff_2_q), .T(t_ff_2_q), .Q(sclk));  // open: Qn, preset, reset, en

  assign cs_2 = cs;

  // Notes on the sheet:
  //   divide by 8
endmodule

module rising_edge (
  input  in_1,
  output out_2
);

  wire not_1_out;

  not not_1 (not_1_out, in_1);
  and and_1 (out_2, in_1, not_1_out);
endmodule

module pc_reset (
  input  in_1,
  input  in_2,
  output out_3
);

  wire not_1_out, rising_edge_1_out_2;

  and and_1 (out_3, in_1, rising_edge_1_out_2);
  not not_1 (not_1_out, in_2);
  rising_edge rising_edge_1 (.in_1(not_1_out), .out_2(rising_edge_1_out_2));
endmodule
