// Logisim project spi_v2.circ as structural Verilog: 4 circuits, main circuit main
module main (
  input  reset,
  input  flush_buffers,
  input  [7:0] pMOSI,
  input  write,
  input  clk,
  input  [1:0] addr,
  input  read,
  output [7:0] pMISO,
  output done
);

  wire _1_byte_sent__1_byte_received_2_out, _1_byte_sent__1_byte_received_2_q6,
       _1_byte_sent__1_byte_received_2_q7, _1_byte_sent__1_byte_received_out, and_1_out, and_2_out,
       and_3_out, cs_q, cs_trigger_q, d_ff_1_q, d_ff_2_q, d_ff_3_q, d_ff_4_q, d_ff_5_q, d_ff_6_q,
       demultiplexer_1_out0, demultiplexer_1_out1, demultiplexer_1_out2, demultiplexer_1_out3,
       falling_edge_1_out_2, falling_edge_2_out_2, falling_edge_3_out_2, fifo_1_contains_data, MISO, MOSI,
       not_1_out, not_2_out, not_3_out, not_4_out, not_5_out, not_6_out, not_7_out, not_8_out, not_9_out,
       not_10_out, nRST, or_1_out, or_2_out, or_3_out, receive_complete_out_2, SCLK, send_complete_out,
       Slave_2_out, Slave_out, SS0, SS1, SS2, SS3, write_pMOSI_q;
  wire [7:0] fifo_1_d_out, random_1_out, Receiver_q0;

  not not_1 (not_1_out, reset);
  FIFO fifo_1 (
    .d_in(pMOSI), .push(d_ff_3_q), .pop(and_3_out), .clock(clk), .contains_data(fifo_1_contains_data),
    .d_out(fifo_1_d_out), .clear(flush_buffers));  // open: full, empty
  FIFO fifo_2 (
    .d_in(Receiver_q0), .push(d_ff_5_q), .pop(d_ff_2_q), .clock(clk), .d_out(pMISO), .clear(flush_buffers));  // open: full, empty, contains_data
  D_Flip_Flop d_ff_1 (.Q(d_ff_1_q), .preset(not_1_out), .reset(write_pMOSI_q));  // open: clk, D, Qn, en
  or or_1 (or_1_out, d_ff_1_q, done);
  D_Flip_Flop d_ff_2 (.clk(read), .D(read), .Q(d_ff_2_q), .reset(falling_edge_1_out_2));  // open: Qn, preset, en
  falling_edge falling_edge_1 (.in_1(clk), .out_2(falling_edge_1_out_2));
  and and_1 (and_1_out, not_3_out, not_8_out);
  assign MISO = and_1_out ? Slave_out : 1'bz;  // Controlled_Buffer controlled_buffer_1
  Shift_Register Slave (
    .shift(not_3_out), .in(MOSI), .clk(not_2_out), .out(Slave_out), .clr(not_4_out));  // open: load, d0, q0, d1, q1, d2, q2, d3, q3, d4, q4, d5, q5, d6, q6, d7, q7
  not not_2 (not_2_out, SCLK);
  Shift_Register #(.length(16)) _1_byte_sent__1_byte_received (
    .shift(not_3_out), .in(1'b1), .clk(not_2_out), .out(_1_byte_sent__1_byte_received_out), .clr(not_4_out));  // open: load, d0, q0, d1, q1, d2, q2, d3, q3, d4, q4, d5, q5, d6, q6, d7, q7, d8, q8, d9, q9, d10, q10, d11, q11, d12, q12, d13, q13, d14, q14, d15, q15
  not not_3 (not_3_out, SS0);
  not not_4 (not_4_out, nRST);
  and and_2 (and_2_out, not_6_out, not_9_out);
  assign MISO = and_2_out ? Slave_2_out : 1'bz;  // Controlled_Buffer controlled_buffer_2
  Shift_Register Slave_2 (
    .shift(not_6_out), .in(MOSI), .clk(not_5_out), .out(Slave_2_out), .load(d_ff_4_q), .clr(not_7_out),
    .d0(random_1_out[0]), .d1(random_1_out[1]), .d2(random_1_out[2]), .d3(random_1_out[3]),
    .d4(random_1_out[4]), .d5(random_1_out[5]), .d6(random_1_out[6]), .d7(random_1_out[7]));  // open: q0, q1, q2, q3, q4, q5, q6, q7
  not not_5 (not_5_out, SCLK);
  not not_6 (not_6_out, SS1);
  Shift_Register #(.length(16)) _1_byte_sent__1_byte_received_2 (
    .shift(not_6_out), .in(1'b1), .clk(not_5_out), .out(_1_byte_sent__1_byte_received_2_out),
    .clr(not_7_out), .q6(_1_byte_sent__1_byte_received_2_q6), .q7(_1_byte_sent__1_byte_received_2_q7));  // open: load, d0, q0, d1, q1, d2, q2, d3, q3, d4, q4, d5, q5, d6, d7, d8, q8, d9, q9, d10, q10, d11, q11, d12, q12, d13, q13, d14, q14, d15, q15
  not not_7 (not_7_out, nRST);
  and and_3 (and_3_out, or_1_out, fifo_1_contains_data);
  D_Flip_Flop d_ff_3 (.clk(write), .D(write), .Q(d_ff_3_q), .reset(falling_edge_2_out_2));  // open: Qn, preset, en
  falling_edge falling_edge_2 (.in_1(clk), .out_2(falling_edge_2_out_2));
  D_Flip_Flop write_pMOSI (.clk(clk), .D(and_3_out), .Q(write_pMOSI_q), .reset(not_1_out));  // open: Qn, preset, en
  D_Flip_Flop cs_trigger (.clk(write), .D(write), .Q(cs_trigger_q), .reset(not_1_out));  // open: Qn, preset, en
  Random random_1 (.clk(SCLK), .out(random_1_out));  // open: next, clr
  D_Flip_Flop d_ff_4 (
    .Q(d_ff_4_q), .preset(_1_byte_sent__1_byte_received_2_q6), .reset(_1_byte_sent__1_byte_received_2_q7));  // open: clk, D, Qn, en
  D_Flip_Flop #(.trigger("falling")) cs (
    .clk(clk), .D(cs_trigger_q), .Q(cs_q), .en(write_pMOSI_q), .reset(or_2_out));  // open: Qn, preset
  or or_2 (or_2_out, not_1_out, done);
  not not_8 (not_8_out, _1_byte_sent__1_byte_received_out);
  not not_9 (not_9_out, _1_byte_sent__1_byte_received_2_out);
  Shift_Register send_complete (
    .shift(cs_q), .in(1'b1), .clk(not_10_out), .out(send_complete_out), .clr(or_3_out));  // open: load, d0, q0, d1, q1, d2, q2, d3, q3, d4, q4, d5, q5, d6, q6, d7, q7
  Shift_Register Sender (
    .shift(cs_q), .in(1'b0), .clk(not_10_out), .out(MOSI), .load(write_pMOSI_q), .clr(not_1_out),
    .d0(fifo_1_d_out[0]), .d1(fifo_1_d_out[1]), .d2(fifo_1_d_out[2]), .d3(fifo_1_d_out[3]),
    .d4(fifo_1_d_out[4]), .d5(fifo_1_d_out[5]), .d6(fifo_1_d_out[6]), .d7(fifo_1_d_out[7]));  // open: q0, q1, q2, q3, q4, q5, q6, q7
  not not_10 (not_10_out, clk);
  Shift_Register Receiver (
    .shift(cs_q), .in(MISO), .clk(clk), .clr(not_1_out), .q0(Receiver_q0[0]), .q1(Receiver_q0[1]),
    .q2(Receiver_q0[2]), .q3(Receiver_q0[3]), .q4(Receiver_q0[4]), .q5(Receiver_q0[5]), .q6(Receiver_q0[6]),
    .q7(Receiver_q0[7]));  // open: out, load, d0, d1, d2, d3, d4, d5, d6, d7
  D_Flip_Flop d_ff_5 (.clk(done), .D(done), .Q(d_ff_5_q), .reset(falling_edge_3_out_2));  // open: Qn, preset, en
  falling_edge falling_edge_3 (.in_1(clk), .out_2(falling_edge_3_out_2));
  or or_3 (or_3_out, not_1_out, write_pMOSI_q);
  and and_4 (SCLK, clk, cs_q);
  is_floating receive_complete (.in_1(MISO), .out_2(receive_complete_out_2));
  Demultiplexer #(.select(2), .disabled(0), .enable("false")) demultiplexer_1 (
    .out0(demultiplexer_1_out0), .out1(demultiplexer_1_out1), .out2(demultiplexer_1_out2),
    .out3(demultiplexer_1_out3), .in(cs_q), .sel(addr));
  D_Flip_Flop d_ff_6 (.clk(clk), .D(send_complete_out), .Q(d_ff_6_q), .reset(not_1_out));  // open: Qn, preset, en
  and and_5 (done, d_ff_6_q, receive_complete_out_2);
  not not_11 (nRST, not_1_out);
  not not_12 (SS0, demultiplexer_1_out0);
  not not_13 (SS1, demultiplexer_1_out1);
  not not_14 (SS2, demultiplexer_1_out2);
  not not_15 (SS3, demultiplexer_1_out3);

  // Notes on the sheet:
  //   in
  //   out
  //   allows write to occur
  //   after reset
  //   write trigger
  //   read trigger
  //   Slave 0
  //   Slave 1
  //   action:
  //   returns byte to master
  //   action:
  //   sends random byte to master
  //   Master
  //   push trigger
  //   if SO is floating and send is
  //   complete, transaction is complete
  //   delay in case SO floats
  //   between write and read
endmodule

module FIFO (
  input  [7:0] d_in,
  input  push,
  input  pop,
  input  clock,
  input  clear,
  output full,
  output empty,
  output contains_data,
  output [7:0] d_out
);

  wire and_1_out, and_2_out, comparator_1_eq, or_1_out, read_addr_carry, t_ff_1_q, t_ff_2_q,
       write_addr_carry, xor_1_out;
  wire [7:0] multiplexer_1_out, multiplexer_2_out, ram_1_data, read_addr_q, write_addr_q;

  and and_1 (and_1_out, pop, ~empty);  // AND_Gate
  and and_2 (and_2_out, push, ~and_1_out);  // AND_Gate
  Counter read_addr (
    .count(and_1_out), .Q(read_addr_q), .carry(read_addr_carry), .clk(clock), .clr(clear));  // open: load, D
  Counter write_addr (
    .count(and_2_out), .Q(write_addr_q), .carry(write_addr_carry), .clk(clock), .clr(clear));  // open: load, D
  T_Flip_Flop t_ff_1 (.clk(read_addr_carry), .T(read_addr_carry), .Q(t_ff_1_q));  // open: Qn, preset, reset, en
  T_Flip_Flop t_ff_2 (.clk(write_addr_carry), .T(write_addr_carry), .Q(t_ff_2_q));  // open: Qn, preset, reset, en
  Multiplexer #(.width(8), .disabled(0), .enable("false")) multiplexer_1 (
    .in0(write_addr_q), .in1(read_addr_q), .out(multiplexer_1_out), .sel(and_1_out));
  xor xor_1 (xor_1_out, t_ff_1_q, t_ff_2_q);
  Comparator comparator_1 (.a(write_addr_q), .b(read_addr_q), .eq(comparator_1_eq));  // open: gt, lt
  not not_1 (contains_data, comparator_1_eq);
  Multiplexer #(.width(8), .disabled(0), .enable("false")) multiplexer_2 (
    .in0(d_in), .in1({8{1'b0}}), .out(multiplexer_2_out), .sel(and_1_out));
  or or_1 (or_1_out, and_2_out, and_1_out);
  and and_3 (full, xor_1_out, comparator_1_eq);
  and and_4 (empty, comparator_1_eq, ~xor_1_out);  // AND_Gate
  RAM #(.bus("separate")) ram_1 (
    .addr(multiplexer_1_out), .din(multiplexer_2_out), .data(ram_1_data), .str(or_1_out), .clk(clock),
    .ld(and_1_out), .clr(clear));  // open: sel
  Register register_1 (.D(ram_1_data), .en(and_1_out), .Q(d_out), .clk(clock), .clr(clear));

  // Notes on the sheet:
  //   in vhdl, instructions will be queued
  //   pop instruction receives priority over push;
  //   if only one address has overflowed
  //   and the lsbs of each address are equal,
  //   then the queue is full
  //   then the queue is empty
  //   if both addresses have overflowed
  //   and the lsbs of each address are equal,
endmodule

module falling_edge (
  input  in_1,
  output out_2
);

  wire not_1_out, not_2_out;

  not not_1 (not_1_out, in_1);
  not not_2 (not_2_out, not_1_out);
  and and_1 (out_2, not_1_out, not_2_out);
endmodule

module is_floating (
  input  in_1,
  output out_2
);

  wire buffer_1_out, buffer_2_out, buffer_3_out, buffer_5_out, not_1_out, pull_resistor_1_node,
       pull_resistor_3_node;

  buf buffer_1 (buffer_1_out, in_1);
  buf buffer_2 (buffer_2_out, in_1);
  Pull_Resistor #(.pull(1)) pull_resistor_1 (.node(pull_resistor_1_node));
  buf buffer_3 (buffer_3_out, buffer_1_out);
  buf buffer_4 (pull_resistor_1_node, buffer_3_out);
  not not_1 (not_1_out, buffer_2_out);
  buf buffer_5 (buffer_5_out, buffer_2_out);
  Pull_Resistor pull_resistor_2 (.node(buffer_2_out));
  Pull_Resistor #(.pull(1)) pull_resistor_3 (.node(pull_resistor_3_node));
  assign pull_resistor_3_node = buffer_5_out ? not_1_out : 1'bz;  // Controlled_Buffer controlled_buffer_1
  and and_1 (out_2, pull_resistor_1_node, pull_resistor_3_node);
endmodule
